// Logisim project PROJECT_X8.circ as structural Verilog: 5 circuits, main circuit main
module main (
);

  wire button_1_out, button_2_out, dipswitch_1_sw1, dipswitch_1_sw2, dipswitch_1_sw3, dipswitch_1_sw4,
       dipswitch_1_sw5, dipswitch_1_sw6, dipswitch_1_sw7, dipswitch_1_sw8, dipswitch_2_sw1, dipswitch_2_sw2,
       dipswitch_2_sw3, dipswitch_2_sw4, dipswitch_2_sw5, dipswitch_2_sw6, dipswitch_2_sw7, dipswitch_2_sw8,
       dipswitch_3_p1, dipswitch_3_p2, dipswitch_3_p3, dipswitch_3_p4, dipswitch_3_p5, dipswitch_3_p6,
       dipswitch_3_p7, dipswitch_3_p8, dipswitch_4_p1, dipswitch_4_p2, dipswitch_4_p3, dipswitch_4_p4,
       dipswitch_4_p5, dipswitch_4_p6, dipswitch_4_p7, dipswitch_4_p8, dipswitch_5_sw1, dipswitch_5_sw2,
       dipswitch_5_sw3, dipswitch_5_sw4, dipswitch_5_sw5, dipswitch_5_sw6, dipswitch_5_sw7, dipswitch_5_sw8,
       dipswitch_6_p1, dipswitch_6_p2, dipswitch_6_p3, dipswitch_6_p4, dipswitch_6_p5, dipswitch_6_p6,
       dipswitch_6_p7, dipswitch_6_p8, i8bit_adder_1_s0, i8bit_adder_1_s1, i8bit_adder_1_s2,
       i8bit_adder_1_s3, i8bit_adder_1_s4, i8bit_adder_1_s5, i8bit_adder_1_s6, i8bit_adder_1_s7,
       i8bit_subs_1_s0, i8bit_subs_1_s1, i8bit_subs_1_s2, i8bit_subs_1_s3, i8bit_subs_1_s4, i8bit_subs_1_s5,
       i8bit_subs_1_s6, i8bit_subs_1_s7, i8bit_subs_2_couta, i8bit_subs_2_couts, i8bit_subs_2_s0,
       i8bit_subs_2_s1, i8bit_subs_2_s2, i8bit_subs_2_s3, i8bit_subs_2_s4, i8bit_subs_2_s5, i8bit_subs_2_s6,
       i8bit_subs_2_s7, srel_1_o;

  DipSwitch dipswitch_1 (
    .sw1(dipswitch_1_sw1), .sw2(dipswitch_1_sw2), .sw3(dipswitch_1_sw3), .sw4(dipswitch_1_sw4),
    .sw5(dipswitch_1_sw5), .sw6(dipswitch_1_sw6), .sw7(dipswitch_1_sw7), .sw8(dipswitch_1_sw8));
  DipSwitch dipswitch_2 (
    .sw1(dipswitch_2_sw1), .sw2(dipswitch_2_sw2), .sw3(dipswitch_2_sw3), .sw4(dipswitch_2_sw4),
    .sw5(dipswitch_2_sw5), .sw6(dipswitch_2_sw6), .sw7(dipswitch_2_sw7), .sw8(dipswitch_2_sw8));
  // DipSwitch dipswitch_3: pin names not known; wires that end beside it: dipswitch_3_p1, dipswitch_3_p2, dipswitch_3_p3, dipswitch_3_p4, dipswitch_3_p5, dipswitch_3_p6, dipswitch_3_p7, dipswitch_3_p8
  // DipSwitch dipswitch_4: pin names not known; wires that end beside it: dipswitch_4_p1, dipswitch_4_p2, dipswitch_4_p3, dipswitch_4_p4, dipswitch_4_p5, dipswitch_4_p6, dipswitch_4_p7, dipswitch_4_p8
  I8bit_subs i8bit_subs_1 (
    .a7(dipswitch_3_p8), .a6(dipswitch_3_p7), .a5(dipswitch_3_p6), .a4(dipswitch_3_p5), .a3(dipswitch_3_p4),
    .a2(dipswitch_3_p3), .a1(dipswitch_3_p2), .a0(dipswitch_3_p1), .b7(dipswitch_1_sw8),
    .b6(dipswitch_1_sw7), .b5(dipswitch_1_sw6), .b4(dipswitch_1_sw5), .b3(dipswitch_1_sw4),
    .b2(dipswitch_1_sw3), .b1(dipswitch_1_sw2), .b0(dipswitch_1_sw1), .flag(1'b0), .CinS(i8bit_subs_2_couts),
    .CinA(i8bit_subs_2_couta), .s7(i8bit_subs_1_s7), .s6(i8bit_subs_1_s6), .s5(i8bit_subs_1_s5),
    .s4(i8bit_subs_1_s4), .s3(i8bit_subs_1_s3), .s2(i8bit_subs_1_s2), .s1(i8bit_subs_1_s1),
    .s0(i8bit_subs_1_s0));  // open: CoutA, CoutS
  I8bit_subs i8bit_subs_2 (
    .a7(dipswitch_4_p8), .a6(dipswitch_4_p7), .a5(dipswitch_4_p6), .a4(dipswitch_4_p5), .a3(dipswitch_4_p4),
    .a2(dipswitch_4_p3), .a1(dipswitch_4_p2), .a0(dipswitch_4_p1), .b7(dipswitch_2_sw8),
    .b6(dipswitch_2_sw7), .b5(dipswitch_2_sw6), .b4(dipswitch_2_sw5), .b3(dipswitch_2_sw4),
    .b2(dipswitch_2_sw3), .b1(dipswitch_2_sw2), .b0(dipswitch_2_sw1), .flag(1'b1), .CinS(1'b0), .CinA(1'b0),
    .CoutA(i8bit_subs_2_couta), .s7(i8bit_subs_2_s7), .s6(i8bit_subs_2_s6), .s5(i8bit_subs_2_s5),
    .s4(i8bit_subs_2_s4), .s3(i8bit_subs_2_s3), .s2(i8bit_subs_2_s2), .s1(i8bit_subs_2_s1),
    .s0(i8bit_subs_2_s0), .CoutS(i8bit_subs_2_couts));
  LED led_1 (.in(i8bit_subs_1_s7));
  LED led_2 (.in(i8bit_subs_1_s6));
  LED led_3 (.in(i8bit_subs_1_s5));
  LED led_4 (.in(i8bit_subs_1_s4));
  LED led_5 (.in(i8bit_subs_1_s3));
  LED led_6 (.in(i8bit_subs_1_s2));
  LED led_7 (.in(i8bit_subs_1_s1));
  LED led_8 (.in(i8bit_subs_1_s0));
  LED led_9 (.in(i8bit_subs_2_s7));
  LED led_10 (.in(i8bit_subs_2_s6));
  LED led_11 (.in(i8bit_subs_2_s5));
  LED led_12 (.in(i8bit_subs_2_s4));
  LED led_13 (.in(i8bit_subs_2_s3));
  LED led_14 (.in(i8bit_subs_2_s2));
  LED led_15 (.in(i8bit_subs_2_s1));
  LED led_16 (.in(i8bit_subs_2_s0));
  Button button_1 (.out(button_1_out));
  Button button_2 (.out(button_2_out));
  DipSwitch dipswitch_5 (
    .sw1(dipswitch_5_sw1), .sw2(dipswitch_5_sw2), .sw3(dipswitch_5_sw3), .sw4(dipswitch_5_sw4),
    .sw5(dipswitch_5_sw5), .sw6(dipswitch_5_sw6), .sw7(dipswitch_5_sw7), .sw8(dipswitch_5_sw8));
  // DipSwitch dipswitch_6: pin names not known; wires that end beside it: dipswitch_6_p1, dipswitch_6_p2, dipswitch_6_p3, dipswitch_6_p4, dipswitch_6_p5, dipswitch_6_p6, dipswitch_6_p7, dipswitch_6_p8
  LED led_17 (.in(srel_1_o));
  SreL srel_1 (.R(button_1_out), .S(button_2_out), .O(srel_1_o));
  I8bit_adder i8bit_adder_1 (
    .a7(dipswitch_6_p8), .a6(dipswitch_6_p7), .a5(dipswitch_6_p6), .a4(dipswitch_6_p5), .a3(dipswitch_6_p4),
    .a2(dipswitch_6_p3), .a1(dipswitch_6_p2), .a0(dipswitch_6_p1), .b7(dipswitch_5_sw8),
    .b6(dipswitch_5_sw7), .b5(dipswitch_5_sw6), .b4(dipswitch_5_sw5), .b3(dipswitch_5_sw4),
    .b2(dipswitch_5_sw3), .b1(dipswitch_5_sw2), .b0(dipswitch_5_sw1), .o_c(1'b0), .s7(i8bit_adder_1_s7),
    .s6(i8bit_adder_1_s6), .s5(i8bit_adder_1_s5), .s4(i8bit_adder_1_s4), .s3(i8bit_adder_1_s3),
    .s2(i8bit_adder_1_s2), .s1(i8bit_adder_1_s1), .s0(i8bit_adder_1_s0));  // open: c
  LED led_18 (.in(i8bit_adder_1_s7));
  LED led_19 (.in(i8bit_adder_1_s6));
  LED led_20 (.in(i8bit_adder_1_s5));
  LED led_21 (.in(i8bit_adder_1_s4));
  LED led_22 (.in(i8bit_adder_1_s3));
  LED led_23 (.in(i8bit_adder_1_s2));
  LED led_24 (.in(i8bit_adder_1_s1));
  LED led_25 (.in(i8bit_adder_1_s0));
endmodule

module f_1bit_adder (
  input  a,
  input  b,
  input  o_c,
  output s,
  output c
);

  wire and_1_out, and_2_out, xor_1_out;

  xor xor_1 (xor_1_out, a, b);
  and and_1 (and_1_out, a, b);
  and and_2 (and_2_out, xor_1_out, o_c);
  xor xor_2 (s, a, b, o_c);
  or or_1 (c, and_1_out, and_2_out);
endmodule

module I8bit_adder (
  input  a7,
  input  a6,
  input  a5,
  input  a4,
  input  a3,
  input  a2,
  input  a1,
  input  a0,
  input  b7,
  input  b6,
  input  b5,
  input  b4,
  input  b3,
  input  b2,
  input  b1,
  input  b0,
  input  o_c,
  output c,
  output s7,
  output s6,
  output s5,
  output s4,
  output s3,
  output s2,
  output s1,
  output s0
);

  wire f_1bit_adder_2_c, f_1bit_adder_3_c, f_1bit_adder_4_c, f_1bit_adder_5_c, f_1bit_adder_6_c,
       f_1bit_adder_7_c, f_1bit_adder_8_c;

  f_1bit_adder f_1bit_adder_1 (.a(a7), .b(b7), .o_c(f_1bit_adder_2_c), .s(s7), .c(c));
  f_1bit_adder f_1bit_adder_2 (.a(a6), .b(b6), .o_c(f_1bit_adder_3_c), .s(s6), .c(f_1bit_adder_2_c));
  f_1bit_adder f_1bit_adder_3 (.a(a5), .b(b5), .o_c(f_1bit_adder_4_c), .s(s5), .c(f_1bit_adder_3_c));
  f_1bit_adder f_1bit_adder_4 (.a(a4), .b(b4), .o_c(f_1bit_adder_5_c), .s(s4), .c(f_1bit_adder_4_c));
  f_1bit_adder f_1bit_adder_5 (.a(a3), .b(b3), .o_c(f_1bit_adder_6_c), .s(s3), .c(f_1bit_adder_5_c));
  f_1bit_adder f_1bit_adder_6 (.a(a2), .b(b2), .o_c(f_1bit_adder_7_c), .s(s2), .c(f_1bit_adder_6_c));
  f_1bit_adder f_1bit_adder_7 (.a(a1), .b(b1), .o_c(f_1bit_adder_8_c), .s(s1), .c(f_1bit_adder_7_c));
  f_1bit_adder f_1bit_adder_8 (.a(a0), .b(b0), .o_c(o_c), .s(s0), .c(f_1bit_adder_8_c));
endmodule

module I8bit_subs (
  input  a7,
  input  a6,
  input  a5,
  input  a4,
  input  a3,
  input  a2,
  input  a1,
  input  a0,
  input  b7,
  input  b6,
  input  b5,
  input  b4,
  input  b3,
  input  b2,
  input  b1,
  input  b0,
  input  flag,
  input  CinS,
  input  CinA,
  output CoutA,
  output s7,
  output s6,
  output s5,
  output s4,
  output s3,
  output s2,
  output s1,
  output s0,
  output CoutS
);

  wire i8bit_adder_1_s0, i8bit_adder_1_s1, i8bit_adder_1_s2, i8bit_adder_1_s3, i8bit_adder_1_s4,
       i8bit_adder_1_s5, i8bit_adder_1_s6, i8bit_adder_1_s7, not_1_out, not_2_out, not_3_out, not_4_out,
       not_5_out, not_6_out, not_7_out, not_8_out;

  not not_1 (not_1_out, b7);
  not not_2 (not_2_out, b6);
  not not_3 (not_3_out, b5);
  not not_4 (not_4_out, b4);
  not not_5 (not_5_out, b3);
  not not_6 (not_6_out, b2);
  not not_7 (not_7_out, b1);
  not not_8 (not_8_out, b0);
  I8bit_adder i8bit_adder_1 (
    .a7(not_1_out), .a6(not_2_out), .a5(not_3_out), .a4(not_4_out), .a3(not_5_out), .a2(not_6_out),
    .a1(not_7_out), .a0(not_8_out), .b7(1'b0), .b6(1'b0), .b5(1'b0), .b4(1'b0), .b3(1'b0), .b2(1'b0),
    .b1(1'b0), .b0(flag), .o_c(CinS), .c(CoutS), .s7(i8bit_adder_1_s7), .s6(i8bit_adder_1_s6),
    .s5(i8bit_adder_1_s5), .s4(i8bit_adder_1_s4), .s3(i8bit_adder_1_s3), .s2(i8bit_adder_1_s2),
    .s1(i8bit_adder_1_s1), .s0(i8bit_adder_1_s0));
  I8bit_adder i8bit_adder_2 (
    .a7(a7), .a6(a6), .a5(a5), .a4(a4), .a3(a3), .a2(a2), .a1(a1), .a0(a0), .b7(i8bit_adder_1_s7),
    .b6(i8bit_adder_1_s6), .b5(i8bit_adder_1_s5), .b4(i8bit_adder_1_s4), .b3(i8bit_adder_1_s3),
    .b2(i8bit_adder_1_s2), .b1(i8bit_adder_1_s1), .b0(i8bit_adder_1_s0), .o_c(CinA), .c(CoutA), .s7(s7),
    .s6(s6), .s5(s5), .s4(s4), .s3(s3), .s2(s2), .s1(s1), .s0(s0));
endmodule

module SreL (
  input  R,
  input  S,
  output O
);

  wire and_1_out, and_2_out, not_1_out;

  not not_1 (not_1_out, R);
  and and_1 (and_1_out, not_1_out, S);
  and and_2 (and_2_out, O, not_1_out);
  or or_1 (O, and_1_out, and_2_out);
endmodule
